# Fritzing sketch Carte_Mat_Balise (saved by Fritzing 0.9.1b)
circuit board: 7cm x 5cm

parts:
  J1 = male pin header, 3 pins [form="♂ (male)"]
  J2 = male pin header, 3 pins [form="♂ (male)"]
  U3 = Voltage Regulator - Variable [part_number=LM1084IT5.0 package="TO220 [THT]"]
  C8 = Tantalum Capacitor [capacitance=10µF package="100 mil [THT, tantalum]"]
  C9 = Tantalum Capacitor [capacitance=10µF package="100 mil [THT, tantalum]"]
  LED4 = LED - 3mm [color="Blue (525nm)" package="3 mm [THT]"]
  R4 = Resistor [tolerance=±5% resistance=1k package=THT]
  R7 = Resistor [tolerance=±5% resistance=1k package=THT]
  R8 = Resistor [tolerance=±5% resistance=1k package=THT]
  J45 = male pin header, 3 pins [form="♂ (male)"]
  R9 = Resistor [tolerance=±5% resistance=1k package=THT]
  LED5 = LED - 3mm [color="Blue (525nm)" package="3 mm [THT]"]
  R11 = Resistor [tolerance=±5% resistance=1k package=THT]
  J44 = screw terminal, 2 pins
  U4 = Voltage Regulator - 5V [part_number="Booster 12 V U3V12F12" package="TO220 [THT]"]
  C10 = Electrolytic Capacitor [capacitance=47µF package="100 mil [THT, electrolytic]"]
  TRINKET1 = Trinket 5V
  J46 = male pin header, 3 pins [form="♂ (male)"]
  R10 = Resistor [tolerance=±20% resistance=1k package=THT]
  R12 = Resistor [tolerance=±20% resistance=1k package=THT]
  J42 = screw terminal, 2 pins

nets:
  N1: J1.pin1, R8.Pin_1
  Alim_Sick: J1.pin2, J45.pin2, U4.output_voltage
  GND: J1.pin3, J2.pin3, U3.ADJ, C8.-, C9.-, R4.Pin_0, R7.Pin_0, J45.pin3, R11.Pin_0, J44.pin2, U4.GND, C10.-, TRINKET1.no_name_yet#2, J46.pin3, R10.Pin_0, J42.pin2
  N2: J2.pin1, R12.Pin_1
  5V: J2.pin2, U3.OUT, C8.+, LED4.anode
  10.8V: U3.IN, C9.+, LED5.anode, J44.pin1, U4.input_voltage, C10.+, TRINKET1.no_name_yet#1, J42.pin1
  N3: LED4.cathode, R4.Pin_1
  SICK_1: R7.Pin_1, R8.Pin_0, TRINKET1.no_name_yet#4
  N4: J45.pin1, R9.Pin_1
  SICK_2: R9.Pin_0, TRINKET1.no_name_yet#3, R10.Pin_1
  N5: LED5.cathode, R11.Pin_1
  Sortie: TRINKET1.no_name_yet#8, J46.pin1
  Servo: TRINKET1.no_name_yet#9, R12.Pin_0

custom parts:
  Trinket 5V: Adafruit Trinket 5V
