# Fritzing sketch Carte_Micro_V3 (saved by Fritzing 0.9.1b)
circuit board: 10cm x 15cm

parts:
  Composant1 = Arduino Micro (Rev3)
  J1 = male pin header, 3 pins [form="♂ (male)"]
  J2 = male pin header, 3 pins [form="♂ (male)"]
  J3 = male pin header, 3 pins [form="♂ (male)"]
  J4 = male pin header, 3 pins [form="♂ (male)"]
  J5 = male pin header, 3 pins [form="♂ (male)"]
  J6 = male pin header, 3 pins [form="♂ (male)"]
  J7 = male pin header, 3 pins [form="♂ (male)"]
  J8 = male pin header, 3 pins [form="♂ (male)"]
  J9 = male pin header, 3 pins [form="♂ (male)"]
  J10 = male pin header, 3 pins [form="♂ (male)"]
  J11 = male pin header, 3 pins [form="♂ (male)"]
  J12 = male pin header, 3 pins [form="♂ (male)"]
  J13 = male pin header, 3 pins [form="♂ (male)"]
  J14 = male pin header, 3 pins [form="♂ (male)"]
  J15 = male pin header, 3 pins [form="♂ (male)"]
  J16 = male pin header, 3 pins [form="♂ (male)"]
  J18 = male pin header, 3 pins [form="♂ (male)"]
  J19 = male pin header, 3 pins [form="♂ (male)"]
  J20 = male pin header, 3 pins [form="♂ (male)"]
  J21 = male pin header, 3 pins [form="♂ (male)"]
  J22 = male pin header, 3 pins [form="♂ (male)"]
  J23 = male pin header, 3 pins [form="♂ (male)"]
  J24 = male pin header, 3 pins [form="♂ (male)"]
  J25 = male pin header, 3 pins [form="♂ (male)"]
  J26 = male pin header, 3 pins [form="♂ (male)"]
  J27 = male pin header, 3 pins [form="♂ (male)"]
  J28 = male pin header, 3 pins [form="♂ (male)"]
  J29 = male pin header, 3 pins [form="♂ (male)"]
  J30 = male pin header, 3 pins [form="♂ (male)"]
  J31 = male pin header, 3 pins [form="♂ (male)"]
  J33 = male pin header, 3 pins [form="♂ (male)"]
  J34 = male pin header, 3 pins [form="♂ (male)"]
  J35 = male pin header, 3 pins [form="♂ (male)"]
  J36 = male pin header, 3 pins [form="♂ (male)"]
  J32 = male pin header, 3 pins [form="♂ (male)"]
  C1 = Capacitor Polarized [package=cpol-radial-100uf-25v]
  C2 = Capacitor Polarized [package=cpol-radial-100uf-25v]
  J37 = male pin header, 4 pins [form="♂ (male)"]
  J38 = male pin header, 4 pins [form="♂ (male)"]
  J39 = male pin header, 2 pins [form="♂ (male)"]
  J40 = male pin header, 2 pins [form="♂ (male)"]
  R1 = Resistor [tolerance=±5% resistance=1k package=THT]
  R2 = Resistor [tolerance=±5% resistance=1k package=THT]
  LED1 = LED - 3mm [color="Orange (605nm)" package="3 mm [THT]"]
  LED2 = LED - 3mm [color="Green (570nm)" package="3 mm [THT]"]
  LED3 = LED - 3mm [color="Blue (525nm)" package="3 mm [THT]"]
  R3 = Resistor [tolerance=±5% resistance=1k package=THT]
  C4 = Tantalum Capacitor [capacitance=10µF package="100 mil [THT, tantalum]"]
  C6 = Tantalum Capacitor [capacitance=10µF package="100 mil [THT, tantalum]"]
  F3 = Resettable Fuse PTC [package=ptc]
  U1 = Voltage Regulator - Variable [part_number=LM1084IT5.0 package="TO220 [THT]"]
  F4 = Resettable Fuse PTC [package=ptc]
  C7 = Tantalum Capacitor [capacitance=10µF package="100 mil [THT, tantalum]"]
  C8 = Tantalum Capacitor [capacitance=10µF package="100 mil [THT, tantalum]"]
  U2 = Voltage Regulator - Variable [part_number=LM1084IT5.0 package="TO220 [THT]"]
  J44 = male pin header, 4 pins [form="♂ (male)"]
  J45 = male pin header, 4 pins [form="♂ (male)"]
  J46 = male pin header, 2 pins [form="♂ (male)"]
  J47 = male pin header, 2 pins [form="♂ (male)"]
  J48 = male pin header, 2 pins [form="♂ (male)"]
  J49 = male pin header, 2 pins [form="♂ (male)"]
  J50 = male pin header, 2 pins [form="♂ (male)"]
  J51 = male pin header, 2 pins [form="♂ (male)"]
  R4 = Resistor [tolerance=±5% resistance=1.5k package=THT]
  R5 = Resistor [tolerance=±5% resistance=1.5k package=THT]
  Pololu_A2 = Pololu A4988 [package=SO16]
  Pololu_A1 = Pololu A4988 [package=SO16]
  J43 = male pin header, 2 pins [form="♂ (male)"]
  J17 = male pin header, 3 pins [form="♂ (male)"]
  J41 = Screw terminal - 2 pins [package=THT]
  J42 = Screw terminal - 2 pins [package=THT]
  F5 = Resettable Fuse PTC [package=ptc]
  C9 = Tantalum Capacitor [capacitance=10µF package="100 mil [THT, tantalum]"]
  C10 = Tantalum Capacitor [capacitance=10µF package="100 mil [THT, tantalum]"]
  U3 = Voltage Regulator - Variable [part_number=LM1084IT5.0 package="TO220 [THT]"]
  LED4 = LED - 3mm [color="Blue (525nm)" package="3 mm [THT]"]
  R6 = Resistor [tolerance=±5% resistance=1k package=THT]
  J52 = male pin header, 3 pins [form="♂ (male)"]
  R7 = Resistor [tolerance=±5% resistance=330 package=THT]
  J53 = male pin header, 3 pins [form="♂ (male)"]
  J54 = male pin header, 3 pins [form="♂ (male)"]
  J55 = male pin header, 3 pins [form="♂ (male)"]
  R8 = Resistor [tolerance=±5% resistance=330 package=THT]
  J56 = male pin header, 3 pins [form="♂ (male)"]
  J57 = male pin header, 3 pins [form="♂ (male)"]
  R9 = Resistor [tolerance=±5% resistance=330 package=THT]
  J58 = male pin header, 3 pins [form="♂ (male)"]
  J59 = male pin header, 3 pins [form="♂ (male)"]
  R10 = Resistor [tolerance=±5% resistance=330 package=THT]
  J60 = male pin header, 3 pins [form="♂ (male)"]
  J61 = male pin header, 3 pins [form="♂ (male)"]
  R11 = Resistor [tolerance=±5% resistance=330 package=THT]
  J62 = male pin header, 3 pins [form="♂ (male)"]
  J63 = male pin header, 3 pins [form="♂ (male)"]
  R12 = Resistor [tolerance=±5% resistance=330 package=THT]
  J64 = male pin header, 3 pins [form="♂ (male)"]
  J65 = male pin header, 3 pins [form="♂ (male)"]
  R13 = Resistor [tolerance=±5% resistance=330 package=THT]
  J66 = male pin header, 3 pins [form="♂ (male)"]
  J67 = male pin header, 3 pins [form="♂ (male)"]
  R14 = Resistor [tolerance=±5% resistance=330 package=THT]
  D1 = Rectifier Diode [part_number=1N4001 package="300 mil [THT]"]
  Composant2 = Arduino Micro (Rev3)
  J68 = double row male pin header, 6 pins [form="♂ (male)"]

nets:
  Ard1_D1: Composant1.D1/TX, J20.pin1
  Ard1_D0: Composant1.D0/RX, J19.pin1
  GND: Composant1.GND, J1.pin3, J2.pin3, J3.pin3, J4.pin3, J5.pin3, J6.pin3, J7.pin3, J8.pin3, J9.pin3, J10.pin3, J11.pin3, J12.pin3, J13.pin3, J14.pin3, J15.pin3, J16.pin3, J18.pin3, J19.pin3, J20.pin3, J21.pin3, J22.pin3, J23.pin3, J24.pin3, J25.pin3, J26.pin3, J27.pin3, J28.pin3, J29.pin3, J30.pin3, J31.pin3, J33.pin3, J34.pin3, J35.pin3, J36.pin3, J32.pin3, C1.-, C2.-, R1.Pin_0, R2.Pin_0, R3.Pin_0, C4.-, C6.-, U1.ADJ, C7.-, C8.-, U2.ADJ, J44.pin4, J45.pin4, J46.pin2, J47.pin2, J48.pin2, J49.pin2, J50.pin2, J51.pin2, Pololu_A2.ENABLE, Pololu_A2.GND, Pololu_A1.ENABLE, Pololu_A1.GND, J17.pin3, J41.pin2, J42.pin2, C9.-, C10.-, U3.ADJ, R6.Pin_0, J53.pin3, J54.pin3, J56.pin3, J58.pin3, J60.pin3, J62.pin3, J64.pin3, J66.pin3, Composant2.GND
  SDA: Composant1.D2/SDA, J44.pin1, J45.pin1, R4.Pin_0, Composant2.D2/SDA
  SCL: Composant1.D3/SCL, J44.pin2, J45.pin2, R5.Pin_0, Composant2.D3/SCL
  Ard1_D4: Composant1.D4_PWM/A6, J24.pin1
  Ard1_D5: Composant1.D5_PWM, J22.pin1
  Ard1_D6: Composant1.D6_PWM/A7, J21.pin1
  Ard1_D7: Composant1.D7, J23.pin1
  Ard1_D8: Composant1.D8_PWM/A8, J25.pin1
  Ard1_D9: Composant1.D9_PWM/A9, J26.pin1
  Ard1_D10: Composant1.D10_PWM/A10, J27.pin1
  Ard1_D11: Composant1.D11_PWM, J28.pin1
  Ard1_D12: Composant1.D12_PWM/A11, J29.pin1
  5V: Composant1.5V, J39.pin1, J40.pin1, LED2.anode, J44.pin3, J45.pin3, R4.Pin_1, R5.Pin_1, J43.pin1, Composant2.5V
  Ard1_A5: Composant1.A5, J31.pin1
  Ard1_A4: Composant1.A4, J32.pin1
  Ard1_A3: Composant1.A3, J33.pin1
  Ard1_A2: Composant1.A2, J34.pin1
  Ard1_A1: Composant1.A1, J35.pin1
  Ard1_A0: Composant1.A0, J36.pin1
  Ard1_D13: Composant1.D13_PWM, J30.pin1
  Ard2_A0: J1.pin1, Composant2.A0
  Alim_Capt_1/Alim_Capt_2/Alim_Sup: J1.pin2, J2.pin2, J3.pin2, J4.pin2, J5.pin2, J6.pin2, J7.pin2, J8.pin2, J9.pin2, J10.pin2, J11.pin2, J12.pin2, J13.pin2, J14.pin2, J15.pin2, J16.pin2, J18.pin2, J19.pin2, J20.pin2, J21.pin2, J22.pin2, J23.pin2, J24.pin2, J25.pin2, J26.pin2, J27.pin2, J28.pin2, J29.pin2, J30.pin2, J31.pin2, J33.pin2, J34.pin2, J35.pin2, J36.pin2, J32.pin2, LED3.anode, F4.2, J46.pin1, J47.pin1, J48.pin1, J49.pin1, J50.pin1, J51.pin1, J17.pin2
  Ard2_A1: J2.pin1, Composant2.A1
  Ard2_A2: J3.pin1, Composant2.A2
  Ard2_A3: J4.pin1, Composant2.A3
  Ard2_A4: J5.pin1, Composant2.A4
  Ard2_A5: J6.pin1, Composant2.A5
  Ard2_D13: J7.pin1, Composant2.D13_PWM
  Ard2_D12: J8.pin1, Pololu_A1.DIR, Composant2.D12_PWM/A11
  Ard2_D11: J9.pin1, Pololu_A1.STEP, Composant2.D11_PWM
  Ard2_D10: J10.pin1, Pololu_A1.SLEEP, Composant2.D10_PWM/A10
  Ard2_D9: J11.pin1, Pololu_A2.DIR, Composant2.D9_PWM/A9
  Ard2_D8: J12.pin1, Pololu_A2.STEP, Composant2.D8_PWM/A8
  Ard2_D4: J13.pin1, Composant2.D4_PWM/A6
  Ard2_D7: J14.pin1, Pololu_A2.SLEEP, Composant2.D7
  Ard2_D5: J15.pin1, Composant2.D5_PWM
  Ard2_D6: J16.pin1, Composant2.D6_PWM/A7
  Ard2_D0: J18.pin1, Composant2.D0/RX
  10V: C1.+, C2.+, LED1.anode, C7.+, U2.IN, Pololu_A2.VMOT, Pololu_A1.VMOT, J41.pin1, J42.pin1, C9.+, U3.IN, D1.anode
  N1: J37.pin1, Pololu_A2.2B
  N2: J37.pin2, Pololu_A2.2A
  N3: J37.pin3, Pololu_A2.1A
  N4: J37.pin4, Pololu_A2.1B
  N5: J38.pin1, Pololu_A1.2B
  N6: J38.pin2, Pololu_A1.2A
  N7: J38.pin3, Pololu_A1.1A
  N8: J38.pin4, Pololu_A1.1B
  N9: J39.pin2, Pololu_A2.VDD
  N10: J40.pin2, Pololu_A1.VDD
  N11: R1.Pin_1, LED1.cathode
  N12: R2.Pin_1, LED2.cathode
  N13: LED3.cathode, R3.Pin_1
  N14: C4.+, F3.1, U1.OUT
  N15: C6.+, U1.IN, D1.cathode
  N16: F3.2, J43.pin2
  N17: F4.1, C8.+, U2.OUT
  MS1: Pololu_A2.MS1, Pololu_A1.MS1, J68.pin3
  MS2: Pololu_A2.MS2, Pololu_A1.MS2, J68.pin2
  MS3: Pololu_A2.MS3, Pololu_A1.MS3, J68.pin1
  Ard2_D1: J17.pin1, Composant2.D1/TX
  N18: F5.1, C10.+, U3.OUT
  Alim_Servo: F5.2, LED4.anode, J53.pin2, J54.pin2, J56.pin2, J58.pin2, J60.pin2, J62.pin2, J64.pin2, J66.pin2
  N19: LED4.cathode, R6.Pin_1
  N20: J52.pin1, R7.Pin_0
  N21: R7.Pin_1, J53.pin1
  N22: J54.pin1, R8.Pin_1
  N23: J55.pin1, R8.Pin_0
  N24: J56.pin1, R9.Pin_1
  N25: J57.pin1, R9.Pin_0
  N26: J58.pin1, R10.Pin_1
  N27: J59.pin1, R10.Pin_0
  N28: J60.pin1, R11.Pin_1
  N29: J61.pin1, R11.Pin_0
  N30: J62.pin1, R12.Pin_1
  N31: J63.pin1, R12.Pin_0
  N32: J64.pin1, R13.Pin_1
  N33: J65.pin1, R13.Pin_0
  N34: J66.pin1, R14.Pin_1
  N35: J67.pin1, R14.Pin_0
  N36: J68.pin4, J68.pin5, J68.pin6

notes:
  Carte_Micro_Robot, Connectique carte
  Carte_Micro_Robot, Arduinos Micro
  Carte_Micro_Robot, Driver Moteur (optimisé pour DRV8834 - Compatible A4988) 
  Carte_Micro_Robot, Regulation tension batterie (de 4.75V à 12V en entrée)
